# Fritzing sketch stepper-motor (saved by Fritzing 0.9.6b)
breadboards: 1

parts:
  YwRobot_Power_Supply1 = YwRobot Breadboard Power Supply [part_number=545043]
  Driver1 = 28BYJ-48 Driver Module [part_number=ULN2003 package=THT]
  SM1 = 28BYJ-48 Stepper Motor [part_number=28BYJ-48]  # not connected
  U2 = ESP8266 NodeMCU LoLin module

nets:
  N1: YwRobot_Power_Supply1.VCC#5, YwRobot_Power_Supply1.VCC#6, U2.Vin
  N2: YwRobot_Power_Supply1.VCC#9, YwRobot_Power_Supply1.VCC#10, Driver1.Vmotor
  N3: YwRobot_Power_Supply1.GND#11, YwRobot_Power_Supply1.GND#12, U2.GND
  N4: YwRobot_Power_Supply1.GND#13, YwRobot_Power_Supply1.GND#14, Driver1.GND
  N5: Driver1.IN1, U2.D1
  N6: Driver1.IN2, U2.D2
  N7: Driver1.IN3, U2.D3
  N8: Driver1.IN4, U2.D4

custom parts:
  YwRobot Breadboard Power Supply: The YwRobot Breadboard Power Supply (MB-V2) has two power rails; they can be 5V or 3V3. Power to the module can be provided through the female USB socket or through the A10 (female) 2.1mm power jack.
  28BYJ-48 Driver Module: High-power ULN2003 Stepper Motor Driver Board Test Module For Arduino AVR SMD
  28BYJ-48 Stepper Motor: Unipolar Stepper Motor 28BYJ-48 Top coil - pink & orange Bottom coil - blue & yellow Common rail - red Connector pins: blue - pink - yellow - orange - red
  ESP8266 NodeMCU LoLin module: ESP8266 based NodeMCU
